// Logisim project Hamming_s encoder _ decoder.circ as structural Verilog: 15 circuits, main circuit encoder
module encoder (
  input  send,
  input  input_1,
  input  input_2,
  input  input_3,
  input  input_4,
  input  reset,
  output x1,
  output x2,
  output x3,
  output x4,
  output x5,
  output x6,
  output x7
);

  wire odd_parity_1_out, odd_parity_2_out, odd_parity_3_out;
  wire [6:0] bit_extender_1_out, bit_extender_2_out;

  xor odd_parity_1 (odd_parity_1_out, input_1, input_2, input_4);
  xor odd_parity_2 (odd_parity_2_out, input_1, input_4, input_3);
  xor odd_parity_3 (odd_parity_3_out, input_3, input_4, input_2);
  assign bit_extender_1_out = {{6{reset}}, reset};  // Bit_Extender bit_extender_1
  S_R_Flip_Flop s_r_ff_1 (
    .S(odd_parity_1_out), .clk(bit_extender_2_out[6]), .R(bit_extender_1_out[0]), .Q(x1),
    .reset(bit_extender_1_out[0]));  // open: Qn, preset, en
  S_R_Flip_Flop s_r_ff_2 (
    .S(odd_parity_2_out), .clk(bit_extender_2_out[5]), .R(bit_extender_1_out[1]), .Q(x2),
    .reset(bit_extender_1_out[1]));  // open: Qn, preset, en
  S_R_Flip_Flop s_r_ff_3 (
    .S(input_1), .clk(bit_extender_2_out[4]), .R(bit_extender_1_out[2]), .Q(x3), .reset(bit_extender_1_out[2]));  // open: Qn, preset, en
  assign bit_extender_2_out = {{6{send}}, send};  // Bit_Extender bit_extender_2
  S_R_Flip_Flop s_r_ff_4 (
    .S(odd_parity_3_out), .clk(bit_extender_2_out[3]), .R(bit_extender_1_out[3]), .Q(x4),
    .reset(bit_extender_1_out[3]));  // open: Qn, preset, en
  S_R_Flip_Flop s_r_ff_5 (
    .S(input_2), .clk(bit_extender_2_out[2]), .R(bit_extender_1_out[4]), .Q(x5), .reset(bit_extender_1_out[4]));  // open: Qn, preset, en
  S_R_Flip_Flop s_r_ff_6 (
    .S(input_4), .clk(bit_extender_2_out[0]), .R(bit_extender_1_out[6]), .Q(x7), .reset(bit_extender_1_out[6]));  // open: Qn, preset, en
  S_R_Flip_Flop s_r_ff_7 (
    .S(input_3), .clk(bit_extender_2_out[1]), .R(bit_extender_1_out[5]), .Q(x6), .reset(bit_extender_1_out[5]));  // open: Qn, preset, en
endmodule

module \wire  (
  input  input_x1,
  input  input_x2,
  input  input_x3,
  input  input_x4,
  input  input_x5,
  input  input_x6,
  input  input_x7,
  input  rand_1,
  input  rand_2,
  input  rand_3,
  input  rand_4,
  input  rand_5,
  input  rand_6,
  input  rand_7,
  output output_x1,
  output output_x2,
  output output_x3,
  output output_x4,
  output output_x5,
  output output_x6,
  output outoput_x7
);

  xor xor_1 (output_x1, rand_1, input_x1);
  xor xor_2 (output_x2, rand_2, input_x2);
  xor xor_3 (output_x3, rand_3, input_x3);
  xor xor_4 (output_x4, rand_4, input_x4);
  xor xor_5 (output_x5, rand_5, input_x5);
  xor xor_6 (output_x6, rand_6, input_x6);
  xor xor_7 (outoput_x7, rand_7, input_x7);
endmodule

module channel (
  input  input_x1,
  input  input_x2,
  input  input_x3,
  input  input_x4,
  input  input_x5,
  input  input_x6,
  input  input_x7,
  input  [6:0] rand_3,
  input  [6:0] rand_2,
  input  [6:0] rand_1,
  output output_x1,
  output output_x2,
  output output_x3,
  output output_x4,
  output output_x5,
  output output_x6,
  output output_x7
);

  wire wire_1_outoput_x7, wire_1_output_x1, wire_1_output_x2, wire_1_output_x3, wire_1_output_x4,
       wire_1_output_x5, wire_1_output_x6, wire_2_outoput_x7, wire_2_output_x1, wire_2_output_x2,
       wire_2_output_x3, wire_2_output_x4, wire_2_output_x5, wire_2_output_x6;

  \wire  wire_1 (
    .input_x1(input_x1), .input_x2(input_x2), .input_x3(input_x3), .input_x4(input_x4), .input_x5(input_x5),
    .input_x6(input_x6), .input_x7(input_x7), .output_x1(wire_1_output_x1), .output_x2(wire_1_output_x2),
    .output_x3(wire_1_output_x3), .output_x4(wire_1_output_x4), .output_x5(wire_1_output_x5),
    .output_x6(wire_1_output_x6), .outoput_x7(wire_1_outoput_x7), .rand_1(rand_1[0]), .rand_2(rand_1[1]),
    .rand_3(rand_1[2]), .rand_4(rand_1[3]), .rand_5(rand_1[4]), .rand_6(rand_1[5]), .rand_7(rand_1[6]));
  \wire  wire_2 (
    .input_x1(wire_1_output_x1), .input_x2(wire_1_output_x2), .input_x3(wire_1_output_x3),
    .input_x4(wire_1_output_x4), .input_x5(wire_1_output_x5), .input_x6(wire_1_output_x6),
    .input_x7(wire_1_outoput_x7), .output_x1(wire_2_output_x1), .output_x2(wire_2_output_x2),
    .output_x3(wire_2_output_x3), .output_x4(wire_2_output_x4), .output_x5(wire_2_output_x5),
    .output_x6(wire_2_output_x6), .outoput_x7(wire_2_outoput_x7), .rand_1(rand_2[0]), .rand_2(rand_2[1]),
    .rand_3(rand_2[2]), .rand_4(rand_2[3]), .rand_5(rand_2[4]), .rand_6(rand_2[5]), .rand_7(rand_2[6]));
  \wire  wire_3 (
    .input_x1(wire_2_output_x1), .input_x2(wire_2_output_x2), .input_x3(wire_2_output_x3),
    .input_x4(wire_2_output_x4), .input_x5(wire_2_output_x5), .input_x6(wire_2_output_x6),
    .input_x7(wire_2_outoput_x7), .output_x1(output_x1), .output_x2(output_x2), .output_x3(output_x3),
    .output_x4(output_x4), .output_x5(output_x5), .output_x6(output_x6), .outoput_x7(output_x7),
    .rand_1(rand_3[0]), .rand_2(rand_3[1]), .rand_3(rand_3[2]), .rand_4(rand_3[3]), .rand_5(rand_3[4]),
    .rand_6(rand_3[5]), .rand_7(rand_3[6]));
endmodule

module LFSR_16bit (
  input  clock,
  output \output 
);

  wire d_ff_1_q, d_ff_2_q, d_ff_3_q, d_ff_4_q, d_ff_5_q, d_ff_6_q, d_ff_7_q, d_ff_8_q, d_ff_9_q, d_ff_10_q,
       d_ff_11_q, d_ff_12_q, d_ff_13_q, d_ff_14_q, d_ff_15_q, x11___x13___x14___x16_out;
  wire [15:0] bit_extender_1_out;

  ExactlyOne x11___x13___x14___x16 (
    .out(x11___x13___x14___x16_out), .in0(\output ), .in1(d_ff_14_q), .in2(d_ff_13_q), .in3(d_ff_11_q));
  D_Flip_Flop d_ff_1 (
    .clk(bit_extender_1_out[0]), .D(x11___x13___x14___x16_out), .Q(d_ff_1_q));  // open: Qn, preset, en, reset
  assign bit_extender_1_out = {{15{clock}}, clock};  // Bit_Extender bit_extender_1
  D_Flip_Flop d_ff_2 (.clk(bit_extender_1_out[1]), .D(d_ff_1_q), .Q(d_ff_2_q));  // open: Qn, preset, en, reset
  D_Flip_Flop d_ff_3 (.clk(bit_extender_1_out[2]), .D(d_ff_2_q), .Q(d_ff_3_q));  // open: Qn, preset, en, reset
  D_Flip_Flop d_ff_4 (.clk(bit_extender_1_out[3]), .D(d_ff_3_q), .Q(d_ff_4_q));  // open: Qn, preset, en, reset
  D_Flip_Flop d_ff_5 (.clk(bit_extender_1_out[4]), .D(d_ff_4_q), .Q(d_ff_5_q));  // open: Qn, preset, en, reset
  D_Flip_Flop d_ff_6 (.clk(bit_extender_1_out[5]), .D(d_ff_5_q), .Q(d_ff_6_q));  // open: Qn, preset, en, reset
  D_Flip_Flop d_ff_7 (.clk(bit_extender_1_out[6]), .D(d_ff_6_q), .Q(d_ff_7_q));  // open: Qn, preset, en, reset
  D_Flip_Flop d_ff_8 (.clk(bit_extender_1_out[7]), .D(d_ff_7_q), .Q(d_ff_8_q));  // open: Qn, preset, en, reset
  D_Flip_Flop d_ff_9 (.clk(bit_extender_1_out[8]), .D(d_ff_8_q), .Q(d_ff_9_q));  // open: Qn, preset, en, reset
  D_Flip_Flop d_ff_10 (.clk(bit_extender_1_out[9]), .D(d_ff_9_q), .Q(d_ff_10_q));  // open: Qn, preset, en, reset
  D_Flip_Flop d_ff_11 (.clk(bit_extender_1_out[10]), .D(d_ff_10_q), .Q(d_ff_11_q));  // open: Qn, preset, en, reset
  D_Flip_Flop d_ff_12 (.clk(bit_extender_1_out[11]), .D(d_ff_11_q), .Q(d_ff_12_q));  // open: Qn, preset, en, reset
  D_Flip_Flop d_ff_13 (.clk(bit_extender_1_out[12]), .D(d_ff_12_q), .Q(d_ff_13_q));  // open: Qn, preset, en, reset
  D_Flip_Flop d_ff_14 (.clk(bit_extender_1_out[13]), .D(d_ff_13_q), .Q(d_ff_14_q));  // open: Qn, preset, en, reset
  D_Flip_Flop d_ff_15 (.clk(bit_extender_1_out[14]), .D(d_ff_14_q), .Q(d_ff_15_q));  // open: Qn, preset, en, reset
  D_Flip_Flop d_ff_16 (.clk(bit_extender_1_out[15]), .D(d_ff_15_q), .Q(\output ));  // open: Qn, preset, en, reset
endmodule

module LFSR_3bit (
  input  clock,
  output \output 
);

  wire d_ff_1_q, d_ff_2_q, x1___x3_out;
  wire [2:0] bit_extender_1_out;

  xor x1___x3 (x1___x3_out, \output , d_ff_1_q);
  D_Flip_Flop d_ff_1 (.clk(bit_extender_1_out[0]), .D(x1___x3_out), .Q(d_ff_1_q));  // open: Qn, preset, en, reset
  assign bit_extender_1_out = {{2{clock}}, clock};  // Bit_Extender bit_extender_1
  D_Flip_Flop d_ff_2 (.clk(bit_extender_1_out[1]), .D(d_ff_1_q), .Q(d_ff_2_q));  // open: Qn, preset, en, reset
  D_Flip_Flop d_ff_3 (.clk(bit_extender_1_out[2]), .D(d_ff_2_q), .Q(\output ));  // open: Qn, preset, en, reset
endmodule

module demux (
  input  input_1,
  input  select_1,
  input  select_2,
  input  select_3,
  output output_1,
  output output_2,
  output output_3,
  output output_4,
  output output_5,
  output output_6,
  output output_7
);

  wire not_1_out, not_2_out, not_3_out;
  wire [6:0] bit_extender_1_out;

  assign bit_extender_1_out = {{6{input_1}}, input_1};  // Bit_Extender bit_extender_1
  not not_1 (not_1_out, select_1);
  not not_2 (not_2_out, select_2);
  not not_3 (not_3_out, select_3);
  and and_1 (output_1, not_1_out, not_2_out, not_3_out, bit_extender_1_out[0]);
  and and_2 (output_2, not_1_out, not_2_out, select_3, bit_extender_1_out[1]);
  and and_3 (output_3, not_1_out, select_2, not_3_out, bit_extender_1_out[2]);
  and and_4 (output_4, not_1_out, select_2, select_3, bit_extender_1_out[3]);
  and and_5 (output_5, select_1, not_2_out, not_3_out, bit_extender_1_out[4]);
  and and_6 (output_6, select_1, not_2_out, select_3, bit_extender_1_out[5]);
  and and_7 (output_7, select_1, select_2, select_3, bit_extender_1_out[6]);
endmodule

module noise_machine (
  input  in_1,
  output [6:0] out_2
);

  wire INPUT_output, not_1_out, not_2_out, not_3_out, Select_1_output, Select_2_output, Select_3_output;
  wire [3:0] bit_extender_1_out;

  assign bit_extender_1_out = {{3{in_1}}, in_1};  // Bit_Extender bit_extender_1
  LFSR_16bit INPUT (.\output (INPUT_output), .clock(bit_extender_1_out[3]));
  not not_1 (not_1_out, bit_extender_1_out[0]);
  not not_2 (not_2_out, bit_extender_1_out[1]);
  not not_3 (not_3_out, bit_extender_1_out[2]);
  LFSR_3bit Select_1 (.\output (Select_1_output), .clock(not_3_out));
  LFSR_3bit Select_2 (.\output (Select_2_output), .clock(not_2_out));
  LFSR_3bit Select_3 (.\output (Select_3_output), .clock(not_1_out));
  demux demux_1 (
    .input_1(INPUT_output), .output_1(out_2[0]), .output_2(out_2[1]), .output_3(out_2[2]),
    .output_4(out_2[3]), .output_5(out_2[4]), .output_6(out_2[5]), .output_7(out_2[6]),
    .select_1(Select_1_output), .select_2(Select_2_output), .select_3(Select_3_output));
endmodule

module vector_adder__sub (
  input  x1,
  input  h1,
  input  x2,
  input  h2,
  input  x3,
  input  h3,
  input  x4,
  input  h4,
  input  x5,
  input  h5,
  input  x6,
  input  h6,
  input  x7,
  input  h7,
  output x_h_i
);

  wire and_1_out, and_2_out, and_3_out, and_4_out, and_5_out, and_6_out, and_7_out;

  and and_1 (and_1_out, x1, h1);
  and and_2 (and_2_out, x2, h2);
  and and_3 (and_3_out, x3, h3);
  and and_4 (and_4_out, x4, h4);
  xor odd_parity_1 (x_h_i, and_1_out, and_2_out, and_3_out, and_4_out, and_5_out, and_6_out, and_7_out);
  and and_5 (and_5_out, x5, h5);
  and and_6 (and_6_out, x6, h6);
  and and_7 (and_7_out, x7, h7);
endmodule

module vector_adder_super (
  input  [6:0] x,
  input  [6:0] h_2,
  input  [6:0] h_3,
  input  [6:0] h_1,
  output error,
  output [2:0] out_6
);

  vector_adder__sub vector_adder__sub_1 (
    .x1(x[0]), .h1(h_1[0]), .x2(x[1]), .h2(h_1[1]), .x3(x[2]), .h3(h_1[2]), .x4(x[3]), .h4(h_1[3]),
    .x5(x[4]), .h5(h_1[4]), .x6(x[5]), .h6(h_1[5]), .x7(x[6]), .h7(h_1[6]), .x_h_i(out_6[0]));
  or or_1 (error, out_6[0], out_6[1], out_6[2]);
  vector_adder__sub vector_adder__sub_2 (
    .x1(x[0]), .h1(h_2[0]), .x2(x[1]), .h2(h_2[1]), .x3(x[2]), .h3(h_2[2]), .x4(x[3]), .h4(h_2[3]),
    .x5(x[4]), .h5(h_2[4]), .x6(x[5]), .h6(h_2[5]), .x7(x[6]), .h7(h_2[6]), .x_h_i(out_6[1]));
  vector_adder__sub vector_adder__sub_3 (
    .x1(x[0]), .h1(h_3[0]), .x2(x[1]), .h2(h_3[1]), .x3(x[2]), .h3(h_3[2]), .x4(x[3]), .h4(h_3[3]),
    .x5(x[4]), .h5(h_3[4]), .x6(x[5]), .h6(h_3[5]), .x7(x[6]), .h7(h_3[6]), .x_h_i(out_6[2]));
endmodule

module error_correcting (
  input  [2:0] error_bit,
  output out_2,
  output out_3,
  output out_4,
  output out_5,
  output out_6,
  output out_7,
  output out_8,
  output out_9
);

  Demultiplexer #(.select(3)) demultiplexer_1 (
    .out0(out_2), .out1(out_3), .out2(out_4), .out3(out_5), .out4(out_6), .out5(out_7), .out6(out_8),
    .out7(out_9), .in(1'b1), .sel(error_bit));  // open: en
endmodule

module parity_check (
  input  x1,
  input  x2,
  input  x3,
  input  x4,
  input  x5,
  input  x6,
  input  x7,
  output error,
  output e_1,
  output e_2,
  output e_3,
  output e_4,
  output e_5,
  output e_6,
  output e_7
);

  wire error_correcting_1_out_2, not_1_out, vector_adder_super_1_error;
  wire [2:0] vector_adder_super_1_out_6;

  vector_adder_super vector_adder_super_1 (
    .x({x7, x6, x5, x4, x3, x2, x1}), .h_3(7'b1111000), .h_2(7'b1100110), .h_1(7'b1010101),
    .error(vector_adder_super_1_error), .out_6(vector_adder_super_1_out_6));
  and and_1 (error, vector_adder_super_1_error, not_1_out);
  not not_1 (not_1_out, error_correcting_1_out_2);
  error_correcting error_correcting_1 (
    .error_bit(vector_adder_super_1_out_6), .out_2(error_correcting_1_out_2), .out_3(e_1), .out_4(e_2),
    .out_5(e_3), .out_6(e_4), .out_7(e_5), .out_8(e_6), .out_9(e_7));
endmodule

module e_i____x (
  input  e_1,
  input  e_2,
  input  e_3,
  input  e_4,
  input  e_5,
  input  e_6,
  input  e_7,
  input  [6:0] x,
  output out_9,
  output out_10,
  output out_11,
  output out_12,
  output out_13,
  output out_14,
  output out_15
);

  xor xor_1 (out_9, x[6], e_1);
  xor xor_2 (out_10, x[5], e_2);
  xor xor_3 (out_11, x[4], e_3);
  xor xor_4 (out_12, x[3], e_4);
  xor xor_5 (out_13, x[2], e_5);
  xor xor_6 (out_14, x[1], e_6);
  xor xor_7 (out_15, x[0], e_7);
endmodule

module decoder (
  input  receive,
  input  y1,
  input  y2,
  input  y3,
  input  y4,
  input  y5,
  input  y6,
  input  y7,
  input  reset,
  output out_10,
  output a4,
  output a3,
  output a2,
  output a1,
  output [2:0] out_15
);

  wire parity_check_1_e_1, parity_check_1_e_2, parity_check_1_e_3, parity_check_1_e_4, parity_check_1_e_5,
       parity_check_1_e_6, parity_check_1_e_7, s_r_ff_1_qn;
  wire [6:0] s_r_ff_6_q;

  S_R_Flip_Flop s_r_ff_1 (
    .S(y2), .clk(receive), .R(reset), .Q(s_r_ff_6_q[5]), .Qn(s_r_ff_1_qn), .reset(reset));  // open: preset, en
  S_R_Flip_Flop s_r_ff_2 (.S(y3), .clk(receive), .R(reset), .Q(s_r_ff_6_q[4]), .reset(reset));  // open: Qn, preset, en
  S_R_Flip_Flop s_r_ff_3 (.S(y4), .clk(receive), .R(reset), .Q(s_r_ff_6_q[3]), .reset(reset));  // open: Qn, preset, en
  S_R_Flip_Flop s_r_ff_4 (.S(y5), .clk(receive), .R(reset), .Q(s_r_ff_6_q[2]), .reset(reset));  // open: Qn, preset, en
  S_R_Flip_Flop s_r_ff_5 (.S(y6), .clk(receive), .R(reset), .Q(s_r_ff_6_q[1]), .reset(reset));  // open: Qn, preset, en
  S_R_Flip_Flop s_r_ff_6 (.S(y7), .clk(receive), .R(reset), .Q(s_r_ff_6_q[0]), .reset(reset));  // open: Qn, preset, en
  S_R_Flip_Flop s_r_ff_7 (.S(y1), .clk(receive), .R(reset), .Q(s_r_ff_6_q[6]), .reset(reset));  // open: Qn, preset, en
  parity_check parity_check_1 (
    .x1(s_r_ff_6_q[6]), .x2(s_r_ff_6_q[5]), .x3(s_r_ff_6_q[4]), .x4(s_r_ff_6_q[3]), .x5(s_r_ff_6_q[2]),
    .x6(s_r_ff_6_q[1]), .x7(s_r_ff_6_q[0]), .error(out_10), .e_1(parity_check_1_e_1),
    .e_2(parity_check_1_e_2), .e_3(parity_check_1_e_3), .e_4(parity_check_1_e_4), .e_5(parity_check_1_e_5),
    .e_6(parity_check_1_e_6), .e_7(parity_check_1_e_7));
  e_i____x e_i_x_1 (
    .e_1(parity_check_1_e_1), .e_2(parity_check_1_e_2), .e_3(parity_check_1_e_3), .e_4(parity_check_1_e_4),
    .e_5(parity_check_1_e_5), .e_6(parity_check_1_e_6), .e_7(parity_check_1_e_7), .x(s_r_ff_6_q),
    .out_9(out_15[2]), .out_10(out_15[1]), .out_11(a1), .out_12(out_15[0]), .out_13(a2), .out_14(a3),
    .out_15(a4));
endmodule

module gate (
  input  [6:0] \input ,
  input  noise_check,
  output [6:0] \output 
);

  and and_1 (\output [0], \input [0], noise_check);
  and and_2 (\output [1], \input [1], noise_check);
  and and_3 (\output [2], \input [2], noise_check);
  and and_4 (\output [3], \input [3], noise_check);
  and and_5 (\output [4], \input [4], noise_check);
  and and_6 (\output [5], \input [5], noise_check);
  and and_7 (\output [6], \input [6], noise_check);
endmodule

module unfaithful_channel (
  input  in_1,
  input  in_2,
  input  in_3,
  input  in_4,
  input  noise_1,
  input  noise_2,
  input  noise_3,
  output out_8,
  output [2:0] out_9,
  output out_10,
  output out_11,
  output out_12,
  output out_13
);

  wire button_1_out, button_2_out, button_3_out, button_4_out, channel_1_output_x1, channel_1_output_x2,
       channel_1_output_x3, channel_1_output_x4, channel_1_output_x5, channel_1_output_x6,
       channel_1_output_x7, clock_1_out, encoder_1_x1, encoder_1_x2, encoder_1_x3, encoder_1_x4,
       encoder_1_x5, encoder_1_x6, encoder_1_x7;
  wire [2:0] bit_extender_1_out;
  wire [6:0] gate_1_output, gate_2_output, gate_3_output, noise_machine_1_out_2, noise_machine_2_out_2,
       noise_machine_3_out_2;

  Button button_1 (.out(button_1_out));
  Button button_2 (.out(button_2_out));
  encoder encoder_1 (
    .send(button_1_out), .input_1(in_1), .input_2(in_2), .input_3(in_3), .input_4(in_4),
    .reset(button_2_out), .x1(encoder_1_x1), .x2(encoder_1_x2), .x3(encoder_1_x3), .x4(encoder_1_x4),
    .x5(encoder_1_x5), .x6(encoder_1_x6), .x7(encoder_1_x7));
  Clock clock_1 (.out(clock_1_out));
  assign bit_extender_1_out = {{2{clock_1_out}}, clock_1_out};  // Bit_Extender bit_extender_1
  gate gate_1 (.\input (noise_machine_1_out_2), .noise_check(noise_1), .\output (gate_1_output));
  noise_machine noise_machine_1 (.out_2(noise_machine_1_out_2), .in_1(bit_extender_1_out[0]));
  channel channel_1 (
    .input_x1(encoder_1_x1), .input_x2(encoder_1_x2), .input_x3(encoder_1_x3), .input_x4(encoder_1_x4),
    .input_x5(encoder_1_x5), .input_x6(encoder_1_x6), .input_x7(encoder_1_x7), .rand_3(gate_3_output),
    .rand_2(gate_2_output), .rand_1(gate_1_output), .output_x1(channel_1_output_x1),
    .output_x2(channel_1_output_x2), .output_x3(channel_1_output_x3), .output_x5(channel_1_output_x5),
    .output_x6(channel_1_output_x6), .output_x7(channel_1_output_x7), .output_x4(channel_1_output_x4));
  gate gate_2 (.\input (noise_machine_2_out_2), .noise_check(noise_2), .\output (gate_2_output));
  noise_machine noise_machine_2 (.out_2(noise_machine_2_out_2), .in_1(bit_extender_1_out[1]));
  gate gate_3 (.\input (noise_machine_3_out_2), .noise_check(noise_3), .\output (gate_3_output));
  noise_machine noise_machine_3 (.out_2(noise_machine_3_out_2), .in_1(bit_extender_1_out[2]));
  decoder decoder_1 (
    .y1(channel_1_output_x1), .y2(channel_1_output_x2), .y3(channel_1_output_x3), .y4(channel_1_output_x4),
    .y5(channel_1_output_x5), .y6(channel_1_output_x6), .y7(channel_1_output_x7), .a4(out_13), .a3(out_12),
    .a2(out_11), .a1(out_10), .out_15(out_9), .out_10(out_8), .receive(button_3_out), .reset(button_4_out));
  Button button_3 (.out(button_3_out));
  Button button_4 (.out(button_4_out));
endmodule
